# Fritzing sketch recepteur_esp32_lora (saved by Fritzing 1.0.3b)
circuit board: 8.46667cm x 5.64444cm

parts:
  JOY-IT = DOIT Esp32 DevKit v1 (30 pins long, 11 pins width) [part_number=ESP32S-PIN30]
  RFM95W1 = RFM95W LoRa Module

nets:
  N1: JOY-IT.3V3, RFM95W1.13_3.3V
  N2: JOY-IT.GND, RFM95W1.8_GND
  N3: JOY-IT.D2, RFM95W1.14_DIO0
  N4: JOY-IT.D5, RFM95W1.5_NSS_(CS)
  N5: JOY-IT.D18, RFM95W1.4_SCK
  N6: JOY-IT.D19, RFM95W1.2_MISO
  N7: JOY-IT.D23, RFM95W1.3_MOSI
  N8: JOY-IT.D14, RFM95W1.6_RESET

custom parts:
  DOIT Esp32 DevKit v1 (30 pins long, 11 pins width): The DOIT Esp32 DevKit v1 is one of the development board created by DOIT to evaluate the ESP-WROOM-32 module. It is based on the ESP32 microcontroller that boasts Wifi, Bluetooth, Ethernet and Low Power support all in a single chip. (vanepp) made breadboard work, adjusted pin numbering and labels and reduced size of schematic and cleaned up pcb. This chip is 30pins long (2 x15) and 11 pins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
  RFM95W LoRa Module: RF Transceiver by Hope RF. Well supported Arduino libraries are available. This Low Power Long Range Transceiver Module for the frequencies 868MHz and 915MHz and it is also available in other versions.
